# Fritzing sketch sketch (saved by Fritzing 0.9.3b)
breadboards: 2

parts:
  DHT1 = DHT22 Humidity and Temperature Sensor
  U3 = LIPO-110mAh [package=lipo-110]
  S1 = Pushbutton [package="[THT]"]
  OLED1 = OLED 128x64 I2C Monochrome Display
  U1 = attiny85 [package=dip]
  R1 = Resistor [tolerance=±5% resistance=10k package=THT]
  U2 = attiny85 [package=dip]
  C1 = Electrolytic Capacitor [capacitance=0.1µF voltage=50V package="100 mil [THT, electrolytic]"]
  Part1 = Arduino Uno (Rev3)

nets:
  VDD: DHT1.VDD, U3.+, S1.Pin_1, S1.Pin_2, OLED1.VDD, U1.Pin_8
  N1: DHT1.DATA, U1.Pin_3
  GND: DHT1.GND, U3.-, OLED1.GND, U1.Pin_4, R1.Pin_1
  N2: S1.Pin_3, S1.Pin_4, U1.Pin_2, R1.Pin_0
  N3: OLED1.SCK, U1.Pin_7
  N4: OLED1.SDA, U1.Pin_5
  N5: U2.Pin_1, Part1.D10_PWM/SS
  N6: U2.Pin_4, C1.-, Part1.GND
  N7: U2.Pin_5, Part1.D11_PWM/MOSI
  N8: U2.Pin_6, Part1.D12/MISO
  N9: U2.Pin_7, Part1.D13/SCK
  N10: U2.Pin_8, Part1.5V
  N11: C1.+, Part1.RESET
